# Fritzing sketch C1011 (saved by Fritzing 0.9.3b)
breadboards: 1

parts:
  U2 = mystery part, 7 pins [chip_label=C1011]
  U1 = NodeMCU V1.0

nets:
  N1: U2.pin1, U1.3V3
  N2: U2.pin2, U1.GND
  N3: U2.pin3, U1.D5
  N4: U2.pin4, U1.D6
  N5: U2.pin5, U1.D7
  N6: U2.pin6, U1.D8
  N7: U2.pin7, U1.D2

custom parts:
  NodeMCU V1.0: ESP8266 based NodeMCU
