# Fritzing sketch CC1101 (saved by Fritzing 0.9.5d)
breadboards: 1

parts:
  U1 = NodeMCU V1.0
  CC1101 = IC, DIP package, 10 pins [chip_label=CC1101]

nets:
  N1: U1.D2, CC1101.pin7
  N2: U1.3V3, CC1101.pin1
  N3: U1.GND, CC1101.pin6
  N4: U1.D5, CC1101.pin9
  N5: U1.D6, CC1101.pin3
  N6: U1.D7, CC1101.pin2
  N7: U1.D8, CC1101.pin4

custom parts:
  NodeMCU V1.0: ESP8266 based NodeMCU
